# Fritzing sketch mount (saved by Fritzing 0.9.3b)
breadboards: 1

parts:
  Part1 = Arduino Nano (Rev3.0)
  Power_plug1 = Power plug
  LED1 = LED - 5mm [color="Red (633nm)" package="5 mm [THT]"]
  LED2 = LED - 5mm [color="Red (633nm)" package="5 mm [THT]"]
  LED3 = LED - 5mm [color="Red (633nm)" package="5 mm [THT]"]
  LED4 = LED - 5mm [color="Red (633nm)" package="5 mm [THT]"]
  LED5 = LED - 5mm [color="Red (633nm)" package="5 mm [THT]"]
  LED6 = LED - 5mm [color="Red (633nm)" package="5 mm [THT]"]
  LED7 = LED - 5mm [color="Red (633nm)" package="5 mm [THT]"]
  LED8 = LED - 5mm [color="Red (633nm)" package="5 mm [THT]"]
  LED9 = LED - 5mm [color="Red (633nm)" package="5 mm [THT]"]
  LED10 = LED - 5mm [color="Red (633nm)" package="5 mm [THT]"]
  U1 = MMA7361 [package=lga14]

nets:
  GND: Part1.GND, Power_plug1.GND, U1.VSS
  N1: Part1.D4, LED10.cathode
  N2: Part1.D5, LED9.cathode
  N3: Part1.D6, LED8.cathode
  N4: Part1.D7, LED7.cathode
  N5: Part1.D8, LED6.cathode
  N6: Part1.D9, LED5.cathode
  N7: Part1.D10, LED4.cathode
  N8: Part1.D11/MOSI, LED3.cathode
  N9: Part1.D12/MISO, LED2.cathode
  5V: Part1.5V, Power_plug1.VCC, LED1.anode, LED2.anode, LED3.anode, LED4.anode, LED5.anode, LED6.anode, LED7.anode, LED8.anode, LED9.anode, LED10.anode, U1.VDD
  N10: Part1.A2, U1.ZOUT
  N11: Part1.A1, U1.YOUT
  N12: Part1.A0, U1.XOUT
  N13: Part1.D13/SCK, LED1.cathode
